// Digital circuit ALU.dig as structural Verilog
module ALU (
  input  [7:0] A,
  input  [7:0] B,
  input  [2:0] ALU_OP,
  output [7:0] RESULT,
  output CARRY,
  output ZERO
);

  wire add_1_c_o, ALU_ADD_c_o, ALU_SUB_c_o, sub_1_c_o;
  wire [7:0] add_1_s, ALU_ADD_s, ALU_SUB_s, and_1_out, not_1_out, or_1_out, sub_1_s, xor_1_out;

  Add #(.Bits(8)) ALU_ADD (.a(A), .b(B), .c_i(1'b0), .s(ALU_ADD_s), .c_o(ALU_ADD_c_o));
  Sub #(.Bits(8)) ALU_SUB (.a(A), .b(B), .c_i(1'b0), .s(ALU_SUB_s), .c_o(ALU_SUB_c_o));
  assign and_1_out = A & B;  // And and_1, 8 bits wide
  assign or_1_out = A | B;  // Or or_1, 8 bits wide
  assign xor_1_out = A ^ B;  // XOr xor_1, 8 bits wide
  assign not_1_out = ~A;  // Not not_1, 8 bits wide
  Add #(.Bits(8)) add_1 (.a(A), .b(8'h1), .c_i(1'b0), .s(add_1_s), .c_o(add_1_c_o));
  Sub #(.Bits(8)) sub_1 (.a(A), .b(8'h1), .c_i(1'b0), .s(sub_1_s), .c_o(sub_1_c_o));
  Multiplexer #(.Selector_Bits(3), .Bits(8)) multiplexer_1 (
    .sel(ALU_OP), .in_0(ALU_ADD_s), .in_1(ALU_SUB_s), .in_2(and_1_out), .in_3(or_1_out), .in_4(xor_1_out),
    .in_5(not_1_out), .in_6(add_1_s), .in_7(sub_1_s), .out(RESULT));
  Multiplexer #(.Selector_Bits(3)) multiplexer_2 (
    .sel(ALU_OP), .in_0(ALU_ADD_c_o), .in_1(ALU_SUB_c_o), .in_2(1'b0), .in_3(1'b0), .in_4(1'b0), .in_5(1'b0),
    .in_6(add_1_c_o), .in_7(sub_1_c_o), .out(CARRY));
  // Probe RESULT on RESULT
  // Probe ALU_SEL on ALU_OP
  Comparator #(.Bits(8)) ZERO_FLAG (.a(RESULT), .b({8{1'b0}}), .eq(ZERO));  // open: gt, lt
endmodule
