// Digital circuit DECODER.dig as structural Verilog
module DECODER (
  input  [3:0] OPCODE,
  input  ZERO,
  input  CARRY,
  input  [1:0] RS,
  output [2:0] ALU_SEL,
  output REG_WE,
  output RAM_CS,
  output RAM_WE,
  output RAM_OE,
  output PC_EN,
  output JUMP_EN,
  output HALT,
  output LOAD_IMM,
  output LOAD_MEM
);

  wire and_1_out, and_3_out, and_4_out, decoder_1_out_3, decoder_1_out_4, decoder_1_out_5, decoder_1_out_6,
       decoder_1_out_7, decoder_1_out_8, decoder_1_out_9, decoder_1_out_10, decoder_1_out_11,
       decoder_1_out_12, decoder_1_out_13, decoder_1_out_14, not_1_out, not_2_out, not_3_out, not_4_out,
       not_5_out, or_5_out;

  not not_1 (not_1_out, HALT);
  and and_1 (and_1_out, not_1_out, not_2_out, not_3_out, decoder_1_out_12);
  not not_2 (not_2_out, decoder_1_out_14);
  not not_3 (not_3_out, decoder_1_out_13);
  Decoder #(.Selector_Bits(4)) decoder_1 (
    .sel(OPCODE), .out_1(RAM_WE), .out_2(LOAD_MEM), .out_3(decoder_1_out_3), .out_4(decoder_1_out_4),
    .out_5(decoder_1_out_5), .out_6(decoder_1_out_6), .out_7(decoder_1_out_7), .out_8(decoder_1_out_8),
    .out_9(decoder_1_out_9), .out_10(decoder_1_out_10), .out_11(decoder_1_out_11), .out_12(decoder_1_out_12),
    .out_13(decoder_1_out_13), .out_14(decoder_1_out_14), .out_15(HALT));  // open: out_0
  not not_4 (not_4_out, RS[0]);
  not not_5 (not_5_out, RS[1]);
  or or_1 (RAM_CS, RAM_WE, LOAD_MEM);
  not not_6 (PC_EN, HALT);
  or or_2 (REG_WE, or_5_out, decoder_1_out_3, decoder_1_out_4, decoder_1_out_5, decoder_1_out_6, decoder_1_out_7, decoder_1_out_8, decoder_1_out_9, decoder_1_out_10, decoder_1_out_11, LOAD_MEM);
  and and_2 (LOAD_IMM, not_4_out, not_5_out, and_1_out);
  and and_3 (and_3_out, RS[0], RS[1], and_1_out);
  and and_4 (and_4_out, decoder_1_out_14, ZERO);
  or or_3 (ALU_SEL[2], decoder_1_out_8, decoder_1_out_9, decoder_1_out_10, decoder_1_out_11);
  or or_4 (JUMP_EN, decoder_1_out_13, and_4_out);
  or or_5 (or_5_out, LOAD_IMM, and_3_out);
  or or_6 (ALU_SEL[0], decoder_1_out_5, decoder_1_out_9, decoder_1_out_10, decoder_1_out_11);
  or or_7 (ALU_SEL[1], decoder_1_out_6, decoder_1_out_7, decoder_1_out_10, decoder_1_out_11);

  assign RAM_OE = LOAD_MEM;

  // Notes on the sheet:
  //   OPCODE: From IR
  //   ZERO: From ALU
  //   CARRY: From ALU
endmodule
