// Digital circuit IR.dig as structural Verilog
module IR (
  input  IR_EN,
  input  [15:0] INSTR_IN,
  input  CLK,
  output [3:0] OPCODE,
  output [1:0] RS,
  output [1:0] RD,
  output [7:0] IMM
);

  Register #(.Bits(16)) REG (.D(INSTR_IN), .C(CLK), .en(IR_EN), .Q({OPCODE, RD, RS, IMM}));
endmodule
