// Logisim project MIP8.circ as structural Verilog
module ALU_SUB (
  input  [7:0] A,
  input  [7:0] B,
  output [7:0] RESULT,
  output BORROW
);

  Subtractor subtractor_1 (.a(A), .b(B), .out(RESULT), .bout(BORROW));  // open: bin
endmodule

module ALU_ADD (
  input  [7:0] A,
  input  [7:0] B,
  output [7:0] RESULT,
  output CARRY
);

  Adder adder_1 (.a(A), .b(B), .out(RESULT), .cout(CARRY));  // open: cin
endmodule

module ALU_AND (
  input  [7:0] A,
  input  [7:0] B,
  input  CONST,
  output [7:0] RESULT,
  output FLAG
);

  assign RESULT = A & B;  // AND_Gate and_1, 8 bits wide

  assign FLAG = CONST;
endmodule

module ALU_OR (
  input  [7:0] A,
  input  [7:0] B,
  input  CONST,
  output [7:0] RESULT,
  output FLAG
);

  assign RESULT = A | B;  // OR_Gate or_1, 8 bits wide

  assign FLAG = CONST;
endmodule

module ALU_XOR (
  input  [7:0] A,
  input  [7:0] B,
  input  CONST,
  output [7:0] RESULT,
  output FLAG
);

  assign RESULT = A ^ B;  // XOR_Gate xor_1, 8 bits wide

  assign FLAG = CONST;
endmodule

module ALU_NOT (
  input  [7:0] A,
  input  CONST,
  output [7:0] RESULT,
  output FLAG
);

  assign RESULT = ~A;  // NOT_Gate not_1, 8 bits wide

  assign FLAG = CONST;
endmodule

module ALU_DEC (
  input  [7:0] A,
  output [7:0] RESULT,
  output FLAG
);

  Subtractor subtractor_1 (.a(A), .b(8'h1), .out(RESULT), .bout(FLAG));  // open: bin
endmodule

module ALU_INC (
  input  [7:0] A,
  output [7:0] RESULT,
  output FLAG
);

  Adder adder_1 (.a(A), .b(8'h1), .out(RESULT), .cout(FLAG));  // open: cin
endmodule
