// Digital circuit MIP8.dig as structural Verilog
module MIP8 (
  input  RESET,
  input  clk
);

  wire alu_1_carry, alu_1_zero, decoder_1_halt, decoder_1_jump_en, decoder_1_load_imm, decoder_1_load_mem,
       decoder_1_pc_en, decoder_1_ram_cs, decoder_1_ram_oe, decoder_1_ram_we, decoder_1_reg_we, or_1_out;
  wire [1:0] ir_1_rd, ir_1_rs;
  wire [2:0] decoder_1_alu_sel;
  wire [3:0] ir_1_opcode;
  wire [7:0] alu_1_result, ir_1_imm, multiplexer_1_out, multiplexer_2_out, multiplexer_3_out, pc_1_pc,
       ram_1_data_out, registerbank_1_rd_data1, registerbank_1_rd_data2;
  wire [15:0] rom_1_d;

  PC pc_1 (
    .RESET(RESET), .CLK(clk), .PC_EN(decoder_1_pc_en), .JUMP_EN(decoder_1_jump_en), .JUMP_ADDR(ir_1_imm),
    .PC(pc_1_pc));
  // Probe PC on pc_1_pc
  ROM #(.bigEndian("true"), .AddrBits(8), .isProgramMemory("true"), .Bits(16)) rom_1 (
    .A(pc_1_pc), .sel(1'b1), .D(rom_1_d));
  // Probe IMM on ir_1_imm
  // Probe Addr on rom_1_d
  IR ir_1 (
    .IR_EN(1'b1), .INSTR_IN(rom_1_d), .CLK(clk), .OPCODE(ir_1_opcode), .RS(ir_1_rs), .RD(ir_1_rd),
    .IMM(ir_1_imm));
  // Probe OPCODE on ir_1_opcode
  // Probe WR_DATA on ir_1_rd
  // Probe RS on ir_1_rs
  RegisterBank registerbank_1 (
    .WE(decoder_1_reg_we), .WR_ADDR(ir_1_rd), .WR_DATA(multiplexer_3_out), .RD_ADDR1(ir_1_rd),
    .RD_ADDR2(ir_1_rs), .clk(clk), .RD_DATA1(registerbank_1_rd_data1), .RD_DATA2(registerbank_1_rd_data2));
  // Probe WR_ADDR on ir_1_rd
  // Probe RD on ir_1_rd
  DECODER decoder_1 (
    .OPCODE(ir_1_opcode), .ZERO(alu_1_zero), .CARRY(alu_1_carry), .RS(ir_1_rs), .ALU_SEL(decoder_1_alu_sel),
    .REG_WE(decoder_1_reg_we), .RAM_CS(decoder_1_ram_cs), .RAM_WE(decoder_1_ram_we),
    .RAM_OE(decoder_1_ram_oe), .PC_EN(decoder_1_pc_en), .JUMP_EN(decoder_1_jump_en), .HALT(decoder_1_halt),
    .LOAD_IMM(decoder_1_load_imm), .LOAD_MEM(decoder_1_load_mem));
  // Probe RD_DATA2 on registerbank_1_rd_data2
  // Probe JMP_EN on decoder_1_jump_en
  // Probe REG_WE on decoder_1_reg_we
  // Probe PC_EN on decoder_1_pc_en
  ALU alu_1 (
    .A(registerbank_1_rd_data1), .B(registerbank_1_rd_data2), .ALU_OP(decoder_1_alu_sel),
    .RESULT(alu_1_result), .CARRY(alu_1_carry), .ZERO(alu_1_zero));
  // Probe RD_DATA1 on registerbank_1_rd_data1
  // Probe RAM_CS on decoder_1_ram_cs
  // Probe ALU_ZERO on alu_1_zero
  // Probe ALU_OP on decoder_1_alu_sel
  Multiplexer #(.Bits(8)) multiplexer_1 (
    .sel(or_1_out), .in_0(registerbank_1_rd_data1), .in_1(ir_1_imm), .out(multiplexer_1_out));
  // Probe RAM_WE on decoder_1_ram_we
  // Probe RAM_OE on decoder_1_ram_oe
  // Probe RAM_ADDR on multiplexer_1_out
  // Probe RAM_DATA_IN on registerbank_1_rd_data1
  RAM ram_1 (
    .CLK(clk), .WE(decoder_1_ram_we), .ADDRESS(multiplexer_1_out), .DATA_IN(registerbank_1_rd_data1),
    .OE(decoder_1_ram_oe), .DATA_OUT(ram_1_data_out));
  // Probe ALU_CARRY on alu_1_carry
  // Probe HALT on decoder_1_halt
  // Probe ALU_RESULT on alu_1_result
  or or_1 (or_1_out, decoder_1_ram_we, decoder_1_load_mem);
  // Probe LOAD_MEM on decoder_1_load_mem
  Multiplexer #(.Bits(8)) multiplexer_2 (
    .sel(decoder_1_load_mem), .in_0(alu_1_result), .in_1(ram_1_data_out), .out(multiplexer_2_out));
  Multiplexer #(.Bits(8)) multiplexer_3 (
    .sel(decoder_1_load_imm), .in_0(multiplexer_2_out), .in_1(ir_1_imm), .out(multiplexer_3_out));
  // Probe MEM_ADDR_SEL on or_1_out
  // Probe LOAD_IMM on decoder_1_load_imm

  // Notes on the sheet:
  //   clk: Hz: 5
  //   contents of rom_1 (hex, n*v repeats v):
  //   1c40,1cd7,2000,3000,c07d,50,cc7d,9*0,5678,15*0,9abc,15*0,3000
  //   ,15*0,c07d,15*0,cc7d
endmodule
