// Digital circuit PC.dig as structural Verilog
module PC (
  input  RESET,
  input  CLK,
  input  PC_EN,
  input  JUMP_EN,
  input  [7:0] JUMP_ADDR,
  output [7:0] PC
);

  wire [7:0] multiplexer_1_out, multiplexer_2_out, PC_ADDER_s;

  Multiplexer #(.Bits(8)) multiplexer_1 (.sel(JUMP_EN), .in_0(PC_ADDER_s), .in_1(JUMP_ADDR), .out(multiplexer_1_out));
  Multiplexer #(.Bits(8)) multiplexer_2 (
    .sel(RESET), .in_0(multiplexer_1_out), .in_1({8{1'b0}}), .out(multiplexer_2_out));
  Register #(.Bits(8)) PC_REG (.D(multiplexer_2_out), .C(CLK), .en(PC_EN), .Q(PC));
  Add #(.Bits(8)) PC_ADDER (.a(PC), .b(8'h1), .c_i(1'b0), .s(PC_ADDER_s));  // open: c_o
endmodule
