// Digital circuit RAM.dig as structural Verilog
module RAM (
  input  CLK,
  input  WE,
  input  [7:0] ADDRESS,
  input  [7:0] DATA_IN,
  input  OE,
  output [7:0] DATA_OUT
);

  // Probe DATA_IN on DATA_IN
  // Probe ADDRESS on ADDRESS
  RAMDualPort #(.AddrBits(8), .Bits(8)) ramdualport_1 (
    .A(ADDRESS), .Din(DATA_IN), .str(WE), .C(CLK), .ld(OE), .D(DATA_OUT));
  // Probe DATA_OUT on DATA_OUT
endmodule
