// Digital circuit RegisterBank.dig as structural Verilog
module RegisterBank (
  input  WE,
  input  [1:0] WR_ADDR,
  input  [7:0] WR_DATA,
  input  [1:0] RD_ADDR1,
  input  [1:0] RD_ADDR2,
  input  clk,
  output [7:0] RD_DATA1,
  output [7:0] RD_DATA2
);

  wire and_1_out, and_2_out, and_3_out, and_4_out, decoder_1_out_0, decoder_1_out_1, decoder_1_out_2,
       decoder_1_out_3;
  wire [7:0] REG_1_q, REG_2_q, REG_3_q, REG_4_q;

  Decoder #(.Selector_Bits(2)) decoder_1 (
    .sel(WR_ADDR), .out_0(decoder_1_out_0), .out_1(decoder_1_out_1), .out_2(decoder_1_out_2),
    .out_3(decoder_1_out_3));
  and and_1 (and_1_out, decoder_1_out_0, WE);
  and and_2 (and_2_out, decoder_1_out_1, WE);
  and and_3 (and_3_out, decoder_1_out_2, WE);
  and and_4 (and_4_out, decoder_1_out_3, WE);
  Register #(.Bits(8)) REG_1 (.D(WR_DATA), .C(clk), .en(and_1_out), .Q(REG_1_q));
  Register #(.Bits(8)) REG_2 (.D(WR_DATA), .C(clk), .en(and_2_out), .Q(REG_2_q));
  Register #(.Bits(8)) REG_3 (.D(WR_DATA), .C(clk), .en(and_3_out), .Q(REG_3_q));
  Register #(.Bits(8)) REG_4 (.D(WR_DATA), .C(clk), .en(and_4_out), .Q(REG_4_q));
  // Probe REG_1 on REG_1_q
  // Probe REG_2 on REG_2_q
  // Probe on REG_4_q
  // Probe on REG_3_q
  Multiplexer #(.Selector_Bits(2), .Bits(8)) multiplexer_1 (
    .sel(RD_ADDR1), .in_0(REG_1_q), .in_1(REG_2_q), .in_2(REG_3_q), .in_3(REG_4_q), .out(RD_DATA1));
  Multiplexer #(.Selector_Bits(2), .Bits(8)) multiplexer_2 (
    .sel(RD_ADDR2), .in_0(REG_1_q), .in_1(REG_2_q), .in_2(REG_3_q), .in_3(REG_4_q), .out(RD_DATA2));
endmodule
